# Fritzing sketch Security-Breadboard (saved by Fritzing 0.9.2b)
circuit board: 8.67406cm x 8.20733cm
breadboards: 1

parts:
  Adafruit_HUZZAH_ESP8266_Breakout1 = Adafruit HUZZAH ESP8266 Breakout [part_number=2471]
  USB_Power_in = USB Connectors [package=usb-a-h]
  Adafruit_PIR = PIR sensor
  Q1 = TRANSISTOR_NPN [package=to-92]
  R1 = Resistor [tolerance=±5% resistance=1k package=THT]
  Speaker = SPEAKER [package=pcb_mount_speaker]
  J1 = Screw terminal - 2 pins [package=THT]
  J2 = Screw terminal - 2 pins [package=THT]
  J3 = Screw terminal - 2 pins [package=THT]
  J5 = Screw terminal - 2 pins [package=THT]
  J6 = Screw terminal - 2 pins [package=THT]
  J7 = Screw terminal - 2 pins [package=THT]
  RelayModule_DFR0017_V3_1 = RelayModule DFR0017 V3.1
  TSL2561 = Adafruit TSL2561 [package="SIP (Single Inline) [THT]"]
  S1 = Pushbutton [package="[THT]"]
  R2 = Resistor [tolerance=±5% resistance=470k package=THT]
  C1 = Electrolytic Capacitor [capacitance=0.1mF package="100 mil [THT, electrolytic]"]
  C2 = Ceramic Capacitor [capacitance=100nF package="100 mil [THT, multilayer]"]

nets:
  GND: Adafruit_HUZZAH_ESP8266_Breakout1.GND, USB_Power_in.GND, Adafruit_PIR.GND, Q1.E, J1.pin1, J5.pin2, J6.pin2, RelayModule_DFR0017_V3_1.GND, TSL2561.GND, R2.Pin_1, C1.-, C2.1
  5V: Adafruit_HUZZAH_ESP8266_Breakout1.VBat, USB_Power_in.VBUS, Adafruit_PIR.VDD, Speaker.-, J3.pin1, J5.pin1, J6.pin1, RelayModule_DFR0017_V3_1.5V, C1.+, C2.0
  SDA_Light: Adafruit_HUZZAH_ESP8266_Breakout1.#13, J7.pin2, TSL2561.SDA
  SCL_Light: Adafruit_HUZZAH_ESP8266_Breakout1.#12, J7.pin1, TSL2561.SCL
  N1: Adafruit_HUZZAH_ESP8266_Breakout1.#14, S1.Pin_3, S1.Pin_4, R2.Pin_0
  Relay_On: Adafruit_HUZZAH_ESP8266_Breakout1.#5, RelayModule_DFR0017_V3_1.SIGNAL
  PIR_Signal: Adafruit_HUZZAH_ESP8266_Breakout1.#4, Adafruit_PIR.SIG, J2.pin1
  Alarm_Out: Adafruit_HUZZAH_ESP8266_Breakout1.#15, R1.Pin_1
  3.3V: Adafruit_HUZZAH_ESP8266_Breakout1.3V, J1.pin2, TSL2561.Vin, S1.Pin_1, S1.Pin_2
  N2: Q1.B, R1.Pin_0
  Alarm_Spk: Q1.C, Speaker.+, J3.pin2

notes:
  VCC in
  PIR
  TSL2561
  Speaker
  - +
  - +   in
  + - SDA SCL
  ----------------------------------------------
  The area below the doted line is not on the
  final PCB. Everything below the dotted line
  is placed outside the PCB!

custom parts:
  Adafruit TSL2561: Adafruit TSL2561 Digital Luminosity/Lux/Light Sensor Breakout The TSL2561 luminosity sensor is an advanced digital light sensor, ideal for use in a wide range of light situations. Compared to low cost CdS cells, this sensor is more precise, allowing for exact lux calculations and can be configured for different gain/timing ranges to detect light ranges from up to 0.1 - 40,000+ Lux on the fly.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
