# Fritzing sketch Security (saved by Fritzing 0.9.2b)
breadboards: 1

parts:
  Adafruit_HUZZAH_ESP8266_Breakout1 = Adafruit HUZZAH ESP8266 Breakout [part_number=2471]
  X1 = USB Connectors [package=usb-a-h]
  PIR1 = PIR sensor
  Q1 = TRANSISTOR_NPN [package=to-92]
  R1 = Resistor [tolerance=±5% resistance=1k package=THT]
  SP1 = SPEAKER [package=pcb_mount_speaker]
  Part1 = _TL2561
  RelayModule_DFR1 = RelayModule DFR0017

nets:
  GND: Adafruit_HUZZAH_ESP8266_Breakout1.GND, X1.GND, PIR1.GND, Q1.E, Part1.GND, RelayModule_DFR1.GND
  VDD: Adafruit_HUZZAH_ESP8266_Breakout1.VBat, X1.VBUS, PIR1.VDD, SP1.-, RelayModule_DFR1.5V
  N1: Adafruit_HUZZAH_ESP8266_Breakout1.#13, Part1.SDA
  N2: Adafruit_HUZZAH_ESP8266_Breakout1.#12, Part1.SCL
  N3: Adafruit_HUZZAH_ESP8266_Breakout1.#5, RelayModule_DFR1.Input
  N4: Adafruit_HUZZAH_ESP8266_Breakout1.#4, PIR1.SIG
  N5: Adafruit_HUZZAH_ESP8266_Breakout1.#15, R1.Pin_1
  N6: Adafruit_HUZZAH_ESP8266_Breakout1.3V, Part1.Vcc
  N7: Q1.B, R1.Pin_0
  N8: Q1.C, SP1.+

notes:
  Old version, nw version has different connector!!!!!

custom parts:
  : Sensor de Luminosidade - TL2561
